# Fritzing sketch proje (saved by Fritzing 0.9.3b)
circuit board: 8.46667cm x 5.64444cm
breadboards: 1

parts:
  LCM1602_IIC1 = LCM1602 IIC [part_number="LCM1602 IIC" chip_label="LCM1602 IIC" package="DIP (Dual Inline) [THT]"]
  LCD1 = LCD screen
  LED1 = LED - 5mm [color="Blue (470nm)" package="5 mm [THT]"]
  J1 = Basic Servo
  DS2 = DS18B20 1-Wire Temperature Sensor Probe Cable
  PCB2 = RTC_DS1302_module
  Parça1 = Arduino Uno (Rev3)
  R2 = Resistor [tolerance=±5% resistance=220 package=THT]
  LED2 = LED - 5mm [color="Green (555nm)" package="5 mm [THT]"]
  R3 = Resistor [tolerance=±5% resistance=220 package=THT]
  R4 = Photocell (LDR) [package=THT]
  R5 = Resistor [tolerance=±5% resistance=220 package=THT]
  R6 = Resistor [tolerance=±5% resistance=220 package=THT]
  U1 = SWITCH-SPST-2 [package=switch-spst-vertical]
  JACK1 = 2.1mm Barrel Jack with Terminal Block
  VCC1 = Battery block 9V
  WS2812B1 = WS2812B 12V Strip -- White (60/m)

nets:
  VSS: LCM1602_IIC1.VSS, LCD1.VSS
  VDD: LCM1602_IIC1.VDD, LCD1.VDD
  N1: LCM1602_IIC1.V0, LCD1.V0
  N2: LCM1602_IIC1.RS, LCD1.RS
  N3: LCM1602_IIC1.RW, LCD1.R/W
  N4: LCM1602_IIC1.E, LCD1.E
  N5: LCM1602_IIC1.D0, LCD1.DB0
  N6: LCM1602_IIC1.D1, LCD1.DB1
  N7: LCM1602_IIC1.D2, LCD1.DB2
  N8: LCM1602_IIC1.D3, LCD1.DB3
  N9: LCM1602_IIC1.D4, LCD1.DB4
  N10: LCM1602_IIC1.D5, LCD1.DB5
  N11: LCM1602_IIC1.D6, LCD1.DB6
  N12: LCM1602_IIC1.D7, LCD1.DB7
  N13: LCM1602_IIC1.A, LCD1.LED+
  N14: LCM1602_IIC1.K, LCD1.LED-
  GND: LCM1602_IIC1.GND, LCM1602_IIC1.SDA, J1.gnd, DS2.GND, PCB2.GND, Parça1.A4/SDA, Parça1.GND, R3.Pin_0, R5.Pin_0, R6.Pin_1
  VCC: LCM1602_IIC1.VCC, J1.vcc, DS2.VDD, PCB2.VCC, Parça1.5V, R2.Pin_0, R4.pin_1
  N15: LCM1602_IIC1.SCL, Parça1.A5/SCL
  N16: LCM1602_IIC1.LED_A, LCM1602_IIC1.LED_B
  N17: LED1.anode, Parça1.D2
  N18: J1.pulse, Parça1.D10_PWM/SS
  N19: DS2.shield, Parça1.D13/SCK, R2.Pin_1
  N20: PCB2.RST, Parça1.D8
  N21: PCB2.DAT, Parça1.D7
  N22: PCB2.CLK, Parça1.D6_PWM
  N23: Parça1.A0, R6.Pin_0
  N24: Parça1.D3_PWM, LED2.anode
  N25: Parça1.D4, WS2812B1.GND
  N26: U1.O, VCC1.+, WS2812B1.DI
  N27: U1.P, JACK1.POS
  N28: JACK1.NEG, VCC1.-

notes:
  yemleme aparatı buraya gelecek
  servo motorun sinyal bacağı 10. pine bağlı
  DS18B20 dijital ısı sensörü bu kısım akvaryuma daldırılacak.
  ısı sensörünün sinyal bacağı 13. pine bağlı
  RTC DS1302 modülü lcd ekranda saat bilgisini göstermek ve günde 2 kereyapılacak yemleme saatini ayarlamak için kullanıldı.
  6. pin >>> clock
  7. pin >>> data
  8. pin >>> reset
  2x16 Lcd ile birlikte kullanmış olduğum i2c modülü sayesinde arduino üzerinde daha az pil kullanarak görüntü aldım.
  şerit ledin karta zarar vermemesi için + bacağını direkt güç kaynağına bağladım.
  Taşınabilir olması açısından sisteme hem 9v pil ilehemde adaptör ile güç verilebilecek şekilde ayarladım.
  adaptör ile güç verilmek istenilirse pil gücünü kesmek amacıyla araya buton yerleştirdim.
  şerit ledin - bacağını 4. pine yerleştirerek ldr modül yardımıyla aydınlatmayı kontrol ediyorum.
  Yemleme yapılırken mavi led yanar.
  Sisteme güç verildiğinde yeşil led yanar.
  TARİH BİLGİSİ
  SAAT BİLGİSİ SU SICAKLIĞI BİLGİSİ

custom parts:
  LCM1602 IIC: I2C-Module to use a 1602 or 2004 LCD on with the wire.h libory Serial LCD Modul
  RTC_DS1302_module: Arduino module DS1302 SPI Real Time Clock
  WS2812B 12V Strip -- White (60/m): WS2812B LED Strip, White, 60 pixels per meter, 12V Power

// code stored in the sketch: proje.ino
//=======================================================================================================//|
//                                                                                                       //|
//                          ONDOKUZ MAYIS ÜN?VERS?TES? SAMSUN MESLEK YÜKSEKOKULU                         //|
//                                                                                                       //|
//=======================================================================================================//|
//                                                                                                       //|
//                                  B?LG?SAYAR PROGRAMCILI?I PROGRAMI                                    //|
//                                                                                                       //|
//=======================================================================================================//|
//                                                                                                       //|
//                               GÖMÜLÜ S?STEMLER DERS? F?NAL PROJE ÖDEV?                                //|
//                                                                                                       //|
//=======================================================================================================//|
//                                                                                                       //|
//                                  PROJE ADI: AKVARYUM KONTROL S?STEM?                                  //|
//                                                                                                       //|
//=======================================================================================================//|
//    HAZIRLAYAN: BUSENUR ADIBELL?                                                                       //|
//    Ö?RENC? NO: 20480098                                                                               //|
//                                                                                                       //|
//=======================================================================================================//|
//                                                                                                       //|
//                                               15/06/2021                                              //|
//                                                                                                       //|
//=======================================================================================================//|
//-----------------------------KÜTÜPHANELER--------------------------//
#include <Servo.h>
#include <OneWire.h> // OneWire kütüphane dosyas? ça?r?ld?
#include <DallasTemperature.h>// // DallasTemperature kütüphane dosyas? ça?r?ld?
#include <Wire.h> // wire kütüphanesi ça?r?ld?
#include <LiquidCrystal_I2C.h> // LiquidCrystal_I2C ça?r?ld?
#include <virtuabotixRTC.h>   

//--------------------------------SERVO------------------------------//
//SERVO
Servo motor;  // servoyu tan?mla
 int pos = 0;   
 //--------------------------LEDLER VE BUTON-------------------------//

//#define kled 10  //K?rm?z? led
#define yled 3  //Ye?il led
#define mled 2 //Mavi led
#define sled 4 //?erit led
#define buton 11 // yemleme buton

//--------------------------------------RTC-----------------------------//
int CLK_PIN = 6;                                        //6. pini clock pini olarak tan?mlad?k
int DAT_PIN = 7;                                        //7. pini data pini olarak tan?mlad?k
int RST_PIN = 8;                                        //8. pini reset pini olarak tan?mlad?k.
virtuabotixRTC myRTC(CLK_PIN, DAT_PIN, RST_PIN);        // Kütüphanemizi pinlere at?yoruz.4

//-----------------------------------------LCD--------------------------------------//
int rs = 12, en = 11, d4 = 5, d5 = 4, d6 = 3, d7 = 2;   //LCD'nin pin de?i?kenlerini tan?ml?yoruz.

LiquidCrystal_I2C lcd(0x27,16,2); 

//--------------------------------------SENSÖRLER--------------------------//
#define ONE_WIRE_BUS 13
//Herhangi bir OneWire cihaz?yla ileti?im kurmak için bir oneWire örne?i kuruyoruz.
OneWire oneWire(ONE_WIRE_BUS);

DallasTemperature sensors(&oneWire);

//-----------------------------------START------------------------------------------//
void setup() 
  {  
 Serial.begin(9600); // Seri haberle?meyi ba?latt?m.
  motor.attach(10);// 10. pine servo ba?land?.
 // pinMode(kled, OUTPUT); // k?rm?z? led ç?k?? olarak tan?mland?.
  pinMode(A0, INPUT);
  pinMode(yled, OUTPUT); // ye?il led ç?k?? olarak tan?mland?.
  pinMode(mled, OUTPUT); // mavi led ç?k?? olarak tan?mland?.
  pinMode(sled, OUTPUT); // sar? led ç?k?? olarak tan?mland?.
  pinMode(buton, INPUT); // buton 1 giri? olarak tan?mland?.

  lcd.begin(); // lcd ba?lat?ld?.
  lcd.backlight(); // lcd arka ????? 
  sensors.begin(); //sensörler ba?lat?ld?

   lcd.setCursor(0, 0);
   lcd.print("Proje Sahibi:");
   lcd.setCursor(0, 1);
   lcd.print("Busenur Adibelli");
   delay(2000);
   lcd.clear();
   
   lcd.setCursor(0, 0);
   lcd.print("Ogrenci No:");
   lcd.setCursor(0, 1);
   lcd.print("20480098");
   delay(2000);
   lcd.clear();
}


void loop() 
{
  digitalWrite(yled , HIGH);
  int isik = analogRead(A0); //I??k de?i?kenini A0 pinindeki LDR ile okuyoruz
  Serial.println(isik); //Okunan de?eri seri ileti?im ekran?na yans?t?yoruz
  delay(50);

  if (isik > 450) { //Okunan ???k de?eri 900'den büyük ise
    digitalWrite(sled, HIGH); //LED yanmas?n
  }

  if (isik < 350) { //Okunan ???k de?eri 850'den küçük ise
    digitalWrite(sled, LOW); //LED yans?n
  }
   //SICAKLIK
  sensors.requestTemperatures(); //Bu fonksiyon ile sensöre s?cakl?k okumak istedi?imize ait komutu yollar?z ve sensör s?cakl??? ölçer ve okunmas? için haz?r da bekletir. Her s?cakl?k okunmadan önce bu fonksiyon kullan?lmal?d?r.
  lcd.setCursor(9,1);
  lcd.print(  sensors.getTempCByIndex(0)); //
   lcd.print((char)223);
   lcd.print("C");

  //RTC
   myRTC.updateTime();                                   //RTC'den zaman? okuyoruz
  lcd.setCursor(4,0);                                   //Ekran?n ilk sat?r ilk sütunundan yazmaya ba?l?yoruz.
  lcd.print(myRTC.dayofmonth);                          //Günü ekrana bast?r?yoruz.
  lcd.print("/");
  lcd.print(myRTC.month);                               //Ay? ekrana bast?r?yoruz.
  lcd.print("/");
  lcd.print(myRTC.year);                                //Y?l? ekrana bast?r?yoruz
  lcd.setCursor(0,1);                                  //LCD'nin 2. sat?r 1. sütunundan yazmaya ba?l?yoruz.
  lcd.print(myRTC.hours);                               //Saati ekrana bast?r?yoruz.
  lcd.print(":");
  lcd.print(myRTC.minutes);                             //Dakikayi ekrana bast?r?yoruz.   
  lcd.print(":");
  lcd.print(myRTC.seconds);                             //Saniyeyi ekrana bast?r?yoruz.


   //SERVO
 if (/*myRTC.hours==20  && myRTC.minutes==37&&*/ myRTC.seconds==30)
      {
      
     lcd.clear();
     lcd.print("Yemleniyor");
     digitalWrite(mled , HIGH);
     delay(3000);
     
      motor.write(pos);              // Servo aç? de?eri olarak belirledi?imiz pos de?i?kenini servoya yazd?rd?k.
    delay(15);                       // servonun hedeflenen aç?ya gidebilmesi için 15 ms bekleme ekledik.
  for (pos = 0; pos <= 180; pos += 1) { // For döngüsü ile 0 ile 180 derece aras? gitmesini sa?lad?k.
                                        // her bir ad?mda 1 derece artacak ?ekilde ayarlad?k.
    motor.write(pos);              // Servo aç? de?eri olarak belirledi?imiz pos de?i?kenini servoya yazd?rd?k.
    delay(15);                       // servonun hedeflenen aç?ya gidebilmesi için 15 ms bekleme ekledik.
  } 
  
  lcd.clear();
  lcd.setCursor(0,0);
  lcd.print("Yemleme");
  lcd.setCursor(0,1);
  lcd.print("Tamamlandi.");
   digitalWrite(mled , LOW); 
  delay(2000);
  lcd.clear();
        }  
        
 
 

 

}
